// Logisim project Basic.circ as structural Verilog: 1 circuit, main circuit main
module main (
  input  in,
  input  a,
  input  b,
  input  a_2,
  input  b_2,
  input  a_3,
  input  b_3,
  output out,
  output out_2,
  output out_3,
  output out_4
);

  wire nand_2_out, nand_4_out, nand_5_out, nand_6_out, not_1_out, not_2_out;

  not not_1 (not_1_out, a_2);
  not not_2 (not_2_out, b_2);
  nand nand_1 (out, in, in);
  nand nand_2 (nand_2_out, a, b);
  not not_3 (out_2, nand_2_out);
  nand nand_3 (out_3, not_1_out, not_2_out);
  nand nand_4 (nand_4_out, a_3, b_3);
  nand nand_5 (nand_5_out, a_3, nand_4_out);
  nand nand_6 (nand_6_out, nand_4_out, b_3);
  nand nand_7 (out_4, nand_5_out, nand_6_out);

  // Notes on the sheet:
  //   2. And gate
  //   3. Or gate
  //   4. Xor gate
  //   1. NOT gate (using NAND only)
endmodule
