// Logisim project Basic16.circ as structural Verilog: 1 circuit, main circuit main
module main (
  input  [15:0] in,
  input  [15:0] a,
  input  [15:0] b,
  input  [15:0] a_2,
  input  [15:0] b_2,
  input  [15:0] a_3,
  input  [15:0] b_3,
  output [15:0] out,
  output [15:0] out_2,
  output [15:0] out_3,
  output [15:0] out_4
);

  wire [15:0] nand_2_out, nand_4_out, nand_5_out, nand_6_out, not_1_out, not_2_out;

  assign out = ~(in & in);  // NAND_Gate nand_1, 16 bits wide
  assign nand_2_out = ~(a & b);  // NAND_Gate nand_2, 16 bits wide
  assign not_1_out = ~a_2;  // NOT_Gate not_1, 16 bits wide
  assign not_2_out = ~b_2;  // NOT_Gate not_2, 16 bits wide
  assign out_2 = ~nand_2_out;  // NOT_Gate not_3, 16 bits wide
  assign out_3 = ~(not_1_out & not_2_out);  // NAND_Gate nand_3, 16 bits wide
  assign nand_4_out = ~(a_3 & b_3);  // NAND_Gate nand_4, 16 bits wide
  assign nand_5_out = ~(a_3 & nand_4_out);  // NAND_Gate nand_5, 16 bits wide
  assign nand_6_out = ~(nand_4_out & b_3);  // NAND_Gate nand_6, 16 bits wide
  assign out_4 = ~(nand_5_out & nand_6_out);  // NAND_Gate nand_7, 16 bits wide

  // Notes on the sheet:
  //   1. NOT16 gate (using NAND16 only)
  //   2. And16 gate
  //   3. Or16 gate
  //   4. Xor gate
  //   1. Not16 gate
endmodule
