// Logisim project Mux.circ as structural Verilog: 1 circuit, main circuit main
module main (
  input  a,
  input  sel,
  input  b,
  input  [15:0] a_2,
  input  sel_2,
  input  [15:0] b_2,
  output out,
  output [15:0] out_2
);

  wire and_1_out, and_2_out, bit_extender_2_out, not_1_out;
  wire [15:0] and_3_out, and_4_out, bit_extender_1_out, not_2_out;

  assign bit_extender_1_out = {{15{sel_2}}, sel_2};  // Bit_Extender bit_extender_1
  Bit_Extender #(.in_width(1), .out_width(1)) bit_extender_2 (.in(sel), .out(bit_extender_2_out));
  not not_1 (not_1_out, bit_extender_2_out);
  assign not_2_out = ~bit_extender_1_out;  // NOT_Gate not_2, 16 bits wide
  and and_1 (and_1_out, a, not_1_out);
  and and_2 (and_2_out, bit_extender_2_out, b);
  assign and_3_out = a_2 & not_2_out;  // AND_Gate and_3, 16 bits wide
  assign and_4_out = bit_extender_1_out & b_2;  // AND_Gate and_4, 16 bits wide
  or or_1 (out, and_1_out, and_2_out);
  assign out_2 = and_3_out | and_4_out;  // OR_Gate or_2, 16 bits wide

  // Notes on the sheet:
  //   *Bit Extender
  //   not needed for 1-bit Mux
  //    but  specified in assignment
endmodule
