// Logisim project Or8Way.circ as structural Verilog: 1 circuit, main circuit main
module main (
  input  [7:0] in,
  output out
);

  wire _01_out, _23_out, _45_out, _67_out, _0123_out, _4567_out;

  or _01 (_01_out, in[0], in[1]);
  or _23 (_23_out, in[2], in[3]);
  or _45 (_45_out, in[4], in[5]);
  or _67 (_67_out, in[6], in[7]);
  or _0123 (_0123_out, _01_out, _23_out);
  or _4567 (_4567_out, _45_out, _67_out);
  or or_1 (out, _0123_out, _4567_out);

  // Notes on the sheet:
  //   0123
  //   4567
endmodule
